// Logisim project 1-bit Full Adder.circ as structural Verilog: 1 circuit, main circuit main
module main (
  input  A,
  input  B,
  input  Cin,
  output Output_1,
  output Output_2
);

  wire AND_2_out, AND_out, XOR_out;

  xor XOR (XOR_out, A, B);
  xor XOR_2 (Output_1, XOR_out, Cin);
  and AND (AND_out, Cin, XOR_out);
  and AND_2 (AND_2_out, A, B);
  or OR (Output_2, AND_out, AND_2_out);
endmodule
