// Logisim project 1-bit Half Subtractor.circ as structural Verilog: 1 circuit, main circuit main
module main (
  input  A,
  input  B,
  output out_3,
  output out_4
);

  wire not_1_out;

  not not_1 (not_1_out, A);
  xor xor_1 (out_3, A, B);
  and and_1 (out_4, B, not_1_out);
endmodule
