// Logisim project ALU circuit contains basic operations using multiplexers .circ as structural Verilog: 1 circuit, main circuit main
module main (
  input  [7:0] a,
  input  [7:0] b,
  output [7:0] out_3,
  output [7:0] out_4
);

  wire [7:0] and_1_out, nor_1_out, or_1_out, xor_1_out;

  assign and_1_out = a & b;  // AND_Gate and_1, 8 bits wide
  assign nor_1_out = ~(a | b);  // NOR_Gate nor_1, 8 bits wide
  assign or_1_out = a | b;  // OR_Gate or_1, 8 bits wide
  assign xor_1_out = a ^ b;  // XOR_Gate xor_1, 8 bits wide
  Multiplexer #(.select(4), .width(8)) multiplexer_1 (
    .in1(and_1_out), .in4(nor_1_out), .in10(or_1_out), .in13(xor_1_out), .out(out_3));  // open: in0, in2, in3, in5, in6, in7, in8, in9, in11, in12, in14, in15, sel, en
endmodule
