// Logisim project Eight bit into two parts and perform AND operation on that 4 bit input..circ as structural Verilog: 1 circuit, main circuit main
module main (
  input  [7:0] in_1,
  output [3:0] out_2
);

  assign out_2 = in_1[3:0] & in_1[7:4];  // AND_Gate and_1, 4 bits wide
endmodule
