// Logisim project RAMANDROM.circ as structural Verilog: 1 circuit, main circuit main
module main (
  input  in_1,
  output [7:0] out_2
);

  wire clock_1_out;
  wire [2:0] counter_1_q;
  wire [7:0] rom_1_data;

  Counter #(.width(3), .max('h7)) counter_1 (.Q(counter_1_q), .clk(clock_1_out));  // open: load, D, count, carry, clr
  Clock clock_1 (.out(clock_1_out));
  ROM #(.addrWidth(3)) rom_1 (.addr(counter_1_q), .data(rom_1_data));  // open: sel
  RAM #(.addrWidth(3), .bus("separate")) ram_1 (
    .addr(counter_1_q), .din(rom_1_data), .data(out_2), .clk(clock_1_out), .clr(in_1));  // open: str, sel, ld

  // Notes on the sheet:
  //   contents of rom_1 (hex, n*v repeats v):
  //   a3 b1 1 c2 f1 ee ff aa
endmodule
