// Logisim project compares Two Eight bit numbers..circ as structural Verilog: 1 circuit, main circuit main
module main (
  input  in_1,
  input  in_2,
  input  in_3,
  input  in_4,
  input  in_5,
  input  [7:0] in_6,
  input  in_7,
  input  in_8,
  input  [7:0] in_9,
  input  [7:0] in_10,
  input  in_11,
  input  [7:0] in_12,
  input  in_13,
  input  in_14,
  input  in_15,
  input  in_16
);

  wire comparator_1_eq, comparator_1_gt, comparator_1_lt, comparator_2_eq, comparator_2_gt, comparator_2_lt;
  wire [7:0] undriven;

  Comparator comparator_1 (.a(undriven), .b(in_6), .gt(comparator_1_gt), .eq(comparator_1_eq), .lt(comparator_1_lt));
  Comparator comparator_2 (.a(in_10), .b(in_12), .gt(comparator_2_gt), .eq(comparator_2_eq), .lt(comparator_2_lt));

  assign in_16 = in_14;
endmodule
