// Logisim project splitter to divide .circ as structural Verilog: 2 circuits, main circuit main
module main (
  input  [7:0] in_1
);

  wire decoder_1_a, decoder_1_b, decoder_1_c, decoder_1_d, decoder_1_e, decoder_1_f, decoder_1_g,
       decoder_1_h, decoder_2_a, decoder_2_b, decoder_2_c, decoder_2_d, decoder_2_e, decoder_2_f,
       decoder_2_g, decoder_2_h, decoder_3_a, decoder_3_b, decoder_3_c, decoder_3_d, decoder_3_e,
       decoder_3_f, decoder_3_g, decoder_3_h, decoder_4_a, decoder_4_b, decoder_4_c, decoder_4_d,
       decoder_4_e, decoder_4_f, decoder_4_g, decoder_4_h;

  _7_Segment_Display u_7_segment_display_1 (
    .g(decoder_1_d), .f(decoder_1_c), .a(decoder_1_b), .b(decoder_1_a), .e(decoder_1_e), .d(decoder_1_f),
    .c(decoder_1_g), .dp(decoder_1_h));
  decoder decoder_1 (
    .i1(in_1[7]), .i2(in_1[6]), .a(decoder_1_a), .b(decoder_1_b), .c(decoder_1_c), .d(decoder_1_d),
    .e(decoder_1_e), .f(decoder_1_f), .g(decoder_1_g), .h(decoder_1_h));
  decoder decoder_2 (
    .i1(in_1[5]), .i2(in_1[4]), .a(decoder_2_a), .b(decoder_2_b), .c(decoder_2_c), .d(decoder_2_d),
    .e(decoder_2_e), .f(decoder_2_f), .g(decoder_2_g), .h(decoder_2_h));
  _7_Segment_Display u_7_segment_display_2 (
    .g(decoder_2_d), .f(decoder_2_c), .a(decoder_2_b), .b(decoder_2_a), .e(decoder_2_e), .d(decoder_2_f),
    .c(decoder_2_g), .dp(decoder_2_h));
  _7_Segment_Display u_7_segment_display_3 (
    .g(decoder_3_d), .f(decoder_3_c), .a(decoder_3_b), .b(decoder_3_a), .e(decoder_3_e), .d(decoder_3_f),
    .c(decoder_3_g), .dp(decoder_3_h));
  decoder decoder_3 (
    .i1(in_1[3]), .i2(in_1[2]), .a(decoder_3_a), .b(decoder_3_b), .c(decoder_3_c), .d(decoder_3_d),
    .e(decoder_3_e), .f(decoder_3_f), .g(decoder_3_g), .h(decoder_3_h));
  _7_Segment_Display u_7_segment_display_4 (
    .g(decoder_4_d), .f(decoder_4_c), .a(decoder_4_b), .b(decoder_4_a), .e(decoder_4_e), .d(decoder_4_f),
    .c(decoder_4_g), .dp(decoder_4_h));
  decoder decoder_4 (
    .i1(in_1[1]), .i2(in_1[0]), .a(decoder_4_a), .b(decoder_4_b), .c(decoder_4_c), .d(decoder_4_d),
    .e(decoder_4_e), .f(decoder_4_f), .g(decoder_4_g), .h(decoder_4_h));
endmodule

module decoder (
  input  i1,
  input  i2,
  output a,
  output b,
  output c,
  output d,
  output e,
  output f,
  output g,
  output h
);

  wire not_1_out, not_2_out, not_3_out, not_5_out, not_6_out;

  not not_1 (not_1_out, i2);
  not not_2 (not_2_out, i1);
  not not_3 (not_3_out, i2);
  not not_4 (e, i2);
  not not_5 (not_5_out, i2);
  not not_6 (not_6_out, i1);
  or or_1 (b, not_1_out, i1);
  and and_1 (c, not_2_out, not_3_out);
  or or_2 (f, not_5_out, i1);
  or or_3 (g, not_6_out, i2);

  assign a = 1'b1;
  assign d = i1;
  assign h = 1'b0;
endmodule
